# Fritzing sketch rpi-sensors (saved by Fritzing 0.9.5d)

parts:
  Raspberry_Pi_1 = Raspberry Pi 3 [part_number=RPI-3-V1.2]
  RHT1 = Humidity and Temperature Sensor RHT03
  Q1 = PNP-Transistor [package="TO92 [THT]"]

nets:
  N1: Raspberry_Pi_1.GPIO2, RHT1.Data-signal
  N2: Raspberry_Pi_1.GND, RHT1.GND_1, Q1.C
  N3: Raspberry_Pi_1.GPIO18, Q1.B
  5V: Raspberry_Pi_1.5V, RHT1.Vcc, Q1.E
